# Fritzing sketch diagnosegeraetKLinePlan (saved by Fritzing 0.9.3b)

parts:
  Bauteil2 = Arduino Mega 2560 (Rev3)
  S2 = Round Pushbutton
  S3 = Round Pushbutton
  OLED_128_x_64 = Module display OLED I2C 128x64 SSD1306 [package=THT]
  schwarz = Header 2 [package=molex-1x2_lock]
  blau = Header 2 [package=molex-1x2_lock]
  Buzzer = Piezo Speaker
  LED = LEDs [package=led10mm]
  R1 = Resistor [tolerance=±5% resistance=220 package="2512 [SMD]"]
  10K = Resistor [package="2512 [SMD]"]
  10K_2 = Resistor [package="2512 [SMD]"]
  510_Ohm = Resistor [package="2512 [SMD]"]
  L9637D = DIP - 8 pins [chip_label=L9637D package="DIP (Dual Inline) [THT]"]
  Mod1 = Voltage Sensor 25V
  BC847B = TRANSISTOR_PNP [package=sot23-3]
  1N4148 = Diode [package=diode-1n4148]
  BC847B_2 = TRANSISTOR_PNP [package=sot23-3]
  Stepdown_12V_->_7_2V = RioRand LM2596
  braun = Header 2 [package=molex-1x2_lock]
  510_Ohm_2 = Resistor [package="2512 [SMD]"]
  1K = Resistor [package="2512 [SMD]"]
  1K_2 = Resistor [package="2512 [SMD]"]
  5_6k = Resistor [package="2512 [SMD]"]

nets (from the breadboard view):
  N1: Bauteil2.A0, Mod1.S, Mod1.+
  N2: Bauteil2.D21/SCL, OLED_128_x_64.SCL
  N3: Bauteil2.D20/SDA, OLED_128_x_64.SDA
  N4: Bauteil2.D19/RX1, L9637D.pin5, L9637D.pin6
  N5: Bauteil2.D18/TX1, L9637D.pin8, 1K_2.Pin_0
  GND: Bauteil2.GND, OLED_128_x_64.GND, schwarz.1, Buzzer.pin1, LED.A, 10K.Pin_1, 10K_2.Pin_1, L9637D.V, Mod1.GND, Mod1.-, BC847B.E, BC847B_2.E, Stepdown_12V_->_7_2V.Pin_2, Stepdown_12V_->_7_2V.Pin_4
  N6: Bauteil2.3V3, S2.leg1, S3.leg1
  5V: Bauteil2.5V, OLED_128_x_64.VCC, L9637D.pin7
  N7: Bauteil2.VIN, Stepdown_12V_->_7_2V.Pin_3
  N8: Bauteil2.D3_PWM, Buzzer.pin2
  N9: Bauteil2.D4_PWM, R1.Pin_0
  N10: Bauteil2.D5_PWM, S3.leg0, 10K_2.Pin_0
  N11: Bauteil2.D6_PWM, S2.leg0, 10K.Pin_0
  N12: schwarz.2, 1N4148.A, Stepdown_12V_->_7_2V.Pin_1, 5_6k.Pin_0
  N13: blau.2, Mod1.VCC, 5_6k.Pin_1
  N14: LED.C, R1.Pin_1
  N15: 510_Ohm.Pin_0, L9637D.pin4, BC847B.C, braun.1, 1K.Pin_1
  N16: 510_Ohm.Pin_1, L9637D.pin3, 1N4148.C, 510_Ohm_2.Pin_1
  N17: L9637D.pin2, braun.2, 510_Ohm_2.Pin_0
  N18: BC847B.B, BC847B_2.C, 1K.Pin_0
  N19: BC847B_2.B, 1K_2.Pin_1

notes:
  L9637D
  RX 1 8 LI
  LO 2 7 VS
  VCC 3 6 K
  TX 4 5 GND
  Audi 200 20v
  Diagnosestecker
  + 12V (Sicherung 21)
  - ECU GND
  ECU PIN 55 (K-Line)
  ECU PIN 13 (L-Line)
  ECU PIN 22
  BC847B
  3(C)
  1 (B) 2(E)

custom parts:
  Module display OLED I2C 128x64 SSD1306: Ecran OLED I2C SSD163 de 128x64 avec connexion I2C
  Resistor: Resistor Basic schematic elements and footprints for 0603, 1206, and PTH resistors.
  DIP - 8 pins: A DIP stand-in part for whatever IC you want. With 8 pins on a 300mil dual inline package (DIP) footprint.
